# Fritzing sketch sketch (saved by Fritzing 0.9.2b)
breadboards: 2

parts:
  Part1 = Intel Edison Arduinobreakout
  U1 = LIPO-2000mAh [package=lipo-2000]
  CHARGER1 = USB_LiIon_LiPoly_Charger_v1.2
  Solar_pannel1 = solar_pannel
  PIR1 = PIR sensor
  IC1 = IC, DIP package, 4 pins [chip_label=IC]
  Q1 = Basic FET N-Channel [part_number=RFP30N06L package="TO220 [THT]"]
  Q3 = LTR-301 [package=ltr-301]
  R3 = Resistor [tolerance=±5% resistance=180 package="0402 [SMD]"]
  Q4 = LTR-301 [package=ltr-301]
  R4 = Resistor [tolerance=±5% resistance=180 package="0402 [SMD]"]
  Q5 = LTR-301 [package=ltr-301]
  R5 = Resistor [tolerance=±5% resistance=180 package="0402 [SMD]"]
  Q6 = LTR-301 [package=ltr-301]
  R6 = Resistor [tolerance=±5% resistance=180 package="0402 [SMD]"]
  Q7 = LTR-301 [package=ltr-301]
  R7 = Resistor [tolerance=±5% resistance=180 package="0402 [SMD]"]
  part = Resistor [tolerance=±5% resistance=10k package=THT]

nets:
  N1: Part1.D8, PIR1.SIG
  N2: Part1.D13/SCK, Q1.gate, part.Pin_1
  GND: Part1.GND, PIR1.GND, IC1.pin2, Q1.source, part.Pin_0
  N3: Part1.VIN, IC1.pin1
  N4: U1.+, CHARGER1.batt_plus_1
  N5: U1.-, CHARGER1.batt_minus_1
  N6: CHARGER1.dcin_minus_1, Solar_pannel1.aún_sin_nombre#0
  N7: CHARGER1.dcin_plus_1, Solar_pannel1.aún_sin_nombre#1
  N8: CHARGER1.load_minus_1, IC1.pin3
  N9: CHARGER1.load_plus_1, IC1.pin4
  N10: Q1.drain, Q3.E, Q4.E
  N11: Q3.C, R3.Pin_0
  N12: R3.Pin_1, R4.Pin_1
  N13: Q4.C, R4.Pin_0
  N14: Q5.C, R5.Pin_0
  N15: Q6.C, R6.Pin_0
  N16: Q7.C, R7.Pin_0

notes:
  Step Up to 5V
  10V Step Up
  Light for illuminating the bird nest with IR
  Lithium battery
  Bird's Nest Illumination
  5 x IR LED with 180Ω

custom parts:
  solar_pannel: Solar pannel
